// Digital circuit multiplier_8.dig as structural Verilog
module multiplier_8 (
  input  [7:0] A,
  input  [7:0] B,
  output [7:0] AC_OUT,
  output [7:0] MQ_OUT
);

  wire A0B1, A0B2, A0B3, A0B4, A0B5, A0B6, A0B7, A1B0, A1B1, A1B2, A1B3, A1B4, A1B5, A1B6, A1B7, A2B0, A2B1,
       A2B2, A2B3, A2B4, A2B5, A2B6, A2B7, A3B0, A3B1, A3B2, A3B3, A3B4, A3B5, A3B6, A3B7, A4B0, A4B1, A4B2,
       A4B3, A4B4, A4B5, A4B6, A4B7, A5B0, A5B1, A5B2, A5B3, A5B4, A5B5, A5B6, A5B7, A6B0, A6B1, A6B2, A6B3,
       A6B4, A6B5, A6B6, A6B7, A7B0, A7B1, A7B2, A7B3, A7B4, A7B5, A7B6, A7B7, Cout0, Cout1, Cout2, Cout3,
       Cout4, Cout5, Cout6, Cout7, Cout8, Cout9, Cout10, Cout11, Cout12, Cout13, Cout14, Cout15, Cout16,
       Cout17, Cout18, Cout19, Cout20, Cout21, Cout22, Cout23, Cout24, Cout25, Cout26, Cout27, Cout28,
       Cout29, Cout30, Cout31, Cout32, Cout33, Cout34, Cout35, Cout36, Cout37, Cout38, Cout39, Cout40,
       Cout41, Cout42, Cout43, Cout44, Cout45, Cout46, Cout47, Cout48, SP0, SP1, SP2, SP3, SP4, SP5, SP6,
       SP7, SP8, SP9, SP10, SP11, SP12, SP13, SP14, SP15, SP16, SP17, SP18, SP19, SP20, SP21, SP22, SP23,
       SP24, SP25, SP26, SP27, SP28, SP29, SP30, SP31, SP32, SP33, SP34, SP35;

  and and_1 (A7B7, B[7], A[7]);
  and and_2 (A7B6, B[6], A[7]);
  and and_3 (A6B7, B[7], A[6]);
  and and_4 (A7B5, B[5], A[7]);
  and and_5 (A6B6, B[6], A[6]);
  and and_6 (A5B7, B[7], A[5]);
  and and_7 (A7B4, B[4], A[7]);
  and and_8 (A6B5, B[5], A[6]);
  and and_9 (A5B6, B[6], A[5]);
  and and_10 (A4B7, B[7], A[4]);
  and and_11 (A7B3, B[3], A[7]);
  and and_12 (A6B4, B[4], A[6]);
  and and_13 (A5B5, B[5], A[5]);
  and and_14 (A4B6, B[6], A[4]);
  and and_15 (A3B7, B[7], A[3]);
  and and_16 (A7B2, B[2], A[7]);
  and and_17 (A6B3, B[3], A[6]);
  and and_18 (A5B4, B[4], A[5]);
  and and_19 (A4B5, B[5], A[4]);
  and and_20 (A3B6, B[6], A[3]);
  and and_21 (A2B7, B[7], A[2]);
  and and_22 (A7B1, B[1], A[7]);
  and and_23 (A6B2, B[2], A[6]);
  and and_24 (A5B3, B[3], A[5]);
  and and_25 (A4B4, B[4], A[4]);
  and and_26 (A3B5, B[5], A[3]);
  and and_27 (A2B6, B[6], A[2]);
  and and_28 (A1B7, B[7], A[1]);
  and and_29 (A7B0, B[0], A[7]);
  and and_30 (A6B1, B[1], A[6]);
  and and_31 (A5B2, B[2], A[5]);
  and and_32 (A4B3, B[3], A[4]);
  and and_33 (A3B4, B[4], A[3]);
  and and_34 (A2B5, B[5], A[2]);
  and and_35 (A1B6, B[6], A[1]);
  and and_36 (A0B7, B[7], A[0]);
  and and_37 (A6B0, B[0], A[6]);
  and and_38 (A5B1, B[1], A[5]);
  and and_39 (A4B2, B[2], A[4]);
  and and_40 (A3B3, B[3], A[3]);
  and and_41 (A2B4, B[4], A[2]);
  and and_42 (A1B5, B[5], A[1]);
  and and_43 (A0B6, B[6], A[0]);
  and and_44 (A5B0, B[0], A[5]);
  and and_45 (A4B1, B[1], A[4]);
  and and_46 (A3B2, B[2], A[3]);
  and and_47 (A2B3, B[3], A[2]);
  and and_48 (A1B4, B[4], A[1]);
  and and_49 (A0B5, B[5], A[0]);
  and and_50 (A4B0, B[0], A[4]);
  and and_51 (A3B1, B[1], A[3]);
  and and_52 (A2B2, B[2], A[2]);
  and and_53 (A1B3, B[3], A[1]);
  and and_54 (A0B4, B[4], A[0]);
  and and_55 (A3B0, B[0], A[3]);
  and and_56 (A2B1, B[1], A[2]);
  and and_57 (A1B2, B[2], A[1]);
  and and_58 (A0B3, B[3], A[0]);
  and and_59 (A2B0, B[0], A[2]);
  and and_60 (A1B1, B[1], A[1]);
  and and_61 (A0B2, B[2], A[0]);
  and and_62 (A1B0, B[0], A[1]);
  and and_63 (A0B1, B[1], A[0]);
  and and_64 (AC_OUT[0], B[0], A[1]);
  // full_adder_1bit A1B0__plus__A0B1: pin names not known; wires that end beside it: A1B0, A0B1, 1'b0, AC_OUT[1], Cout0
  // full_adder_1bit A2B0__plus__A1B1: pin names not known; wires that end beside it: A2B0, A1B1, Cout0, SP0, Cout1
  // full_adder_1bit A3B0__plus__A2B1: pin names not known; wires that end beside it: A3B0, A2B1, Cout1, SP1, Cout3
  // full_adder_1bit A4B0__plus__A3B1: pin names not known; wires that end beside it: A4B0, A3B1, Cout3, SP3, Cout6
  // full_adder_1bit A5B0__plus__A4B1: pin names not known; wires that end beside it: A5B0, A4B1, Cout6, SP6, Cout10
  // full_adder_1bit A6B0__plus__A5B1: pin names not known; wires that end beside it: A6B0, A5B1, Cout10, SP10, Cout15
  // full_adder_1bit A7B0__plus__A6B1: pin names not known; wires that end beside it: A7B0, A6B1, Cout15, SP15, Cout21
  // full_adder_1bit A7B1__plus__A6B2: pin names not known; wires that end beside it: A7B1, A6B2, Cout21, SP21, Cout28
  // full_adder_1bit A7B2__plus__A6B3: pin names not known; wires that end beside it: A7B2, A6B3, Cout28, SP26, Cout34
  // full_adder_1bit A7B3__plus__A6B4: pin names not known; wires that end beside it: A7B3, A6B4, Cout34, SP30, Cout39
  // full_adder_1bit A7B4__plus__A6B5: pin names not known; wires that end beside it: A7B4, A6B5, Cout39, SP33, Cout43
  // full_adder_1bit A7B5__plus__A6B6: pin names not known; wires that end beside it: A7B5, A6B6, Cout43, SP35, Cout46
  // full_adder_1bit full_adder_1bit_1: pin names not known; wires that end beside it: A7B6, A6B7, Cout46, MQ_OUT[5], Cout48
  // full_adder_1bit full_adder_1bit_2: pin names not known; wires that end beside it: A7B7, Cout48, 1'b0, MQ_OUT[6], MQ_OUT[7]
  // full_adder_1bit SP0__plus__A0B2: pin names not known; wires that end beside it: A0B2, SP0, 1'b0, AC_OUT[2], Cout2
  // full_adder_1bit A1B2__plus__SP1: pin names not known; wires that end beside it: A1B2, SP1, Cout2, SP2, Cout4
  // full_adder_1bit A2B2__plus__SP3: pin names not known; wires that end beside it: A2B2, SP3, Cout4, SP4, Cout7
  // full_adder_1bit A3B2__plus__SP6: pin names not known; wires that end beside it: A3B2, SP6, Cout7, SP7, Cout11
  // full_adder_1bit A4B2__plus__SP10: pin names not known; wires that end beside it: A4B2, SP10, Cout11, SP11, Cout16
  // full_adder_1bit A5B2__plus__SP15: pin names not known; wires that end beside it: A5B2, SP15, Cout16, SP16, Cout22
  // full_adder_1bit A5B3__plus__SP21: pin names not known; wires that end beside it: A5B3, SP21, Cout22, SP22, Cout29
  // full_adder_1bit A5B4__plus__SP26: pin names not known; wires that end beside it: A5B4, SP26, Cout29, SP27, Cout35
  // full_adder_1bit A5B5__plus__SP32: pin names not known; wires that end beside it: A5B5, SP30, Cout35, SP31, Cout40
  // full_adder_1bit A5B6__plus__SP35: pin names not known; wires that end beside it: A5B6, SP33, Cout40, SP34, Cout44
  // full_adder_1bit A5B7__plus__SP37: pin names not known; wires that end beside it: A5B7, SP35, Cout44, MQ_OUT[4], Cout47
  // full_adder_1bit A0B3__plus__SP2: pin names not known; wires that end beside it: A0B3, SP2, 1'b0, AC_OUT[3], Cout5
  // full_adder_1bit A1B3__plus__SP4: pin names not known; wires that end beside it: A1B3, SP4, Cout5, SP5, Cout8
  // full_adder_1bit A2B3__plus__SP7: pin names not known; wires that end beside it: A2B3, SP7, Cout8, SP8, Cout12
  // full_adder_1bit A3B3__plus__SP11: pin names not known; wires that end beside it: A3B3, SP11, Cout12, SP12, Cout17
  // full_adder_1bit A4B3__plus__SP16: pin names not known; wires that end beside it: A4B3, SP16, Cout17, SP17, Cout23
  // full_adder_1bit A4B4__plus__SP22: pin names not known; wires that end beside it: A4B4, SP22, Cout23, SP23, Cout30
  // full_adder_1bit A4B5__plus__SP27: pin names not known; wires that end beside it: A4B5, SP27, Cout30, SP28, Cout36
  // full_adder_1bit A4B6__plus__SP33: pin names not known; wires that end beside it: A4B6, SP31, Cout36, SP32, Cout41
  // full_adder_1bit A4B7__plus__SP36: pin names not known; wires that end beside it: A4B7, SP34, Cout41, MQ_OUT[3], Cout45
  // full_adder_1bit A0B4__plus__SP5: pin names not known; wires that end beside it: A0B4, SP5, 1'b0, AC_OUT[4], Cout9
  // full_adder_1bit A1B4__plus__SP8: pin names not known; wires that end beside it: A1B4, SP8, Cout9, SP9, Cout13
  // full_adder_1bit A2B4__plus__SP12: pin names not known; wires that end beside it: A2B4, SP12, Cout13, SP13, Cout18
  // full_adder_1bit A3B4__plus__SP17: pin names not known; wires that end beside it: A3B4, SP17, Cout18, SP18, Cout24
  // full_adder_1bit A3B5__plus__SP23: pin names not known; wires that end beside it: A3B5, SP23, Cout24, SP24, Cout31
  // full_adder_1bit A3B6__plus__SP28: pin names not known; wires that end beside it: A3B6, SP28, Cout31, SP29, Cout37
  // full_adder_1bit A3B7__plus__SP34: pin names not known; wires that end beside it: A3B7, SP32, Cout37, MQ_OUT[2], Cout42
  // full_adder_1bit A0B5__plus__SP9: pin names not known; wires that end beside it: A0B5, SP9, 1'b0, AC_OUT[5], Cout14
  // full_adder_1bit A1B5__plus__SP13: pin names not known; wires that end beside it: A1B5, SP13, Cout14, SP14, Cout19
  // full_adder_1bit A2B5__plus__SP18: pin names not known; wires that end beside it: A2B5, SP18, Cout19, SP19, Cout25
  // full_adder_1bit A2B6__plus__SP24: pin names not known; wires that end beside it: A2B6, SP24, Cout25, SP25, Cout32
  // full_adder_1bit A2B7__plus__SP29: pin names not known; wires that end beside it: A2B7, SP29, Cout32, MQ_OUT[1], Cout38
  // full_adder_1bit A0B6__plus__AP14: pin names not known; wires that end beside it: A0B6, SP14, 1'b0, AC_OUT[6], Cout20
  // full_adder_1bit A1B6__plus__SP19: pin names not known; wires that end beside it: A1B6, SP19, Cout20, SP20, Cout26
  // full_adder_1bit A1B7__plus__SP25: pin names not known; wires that end beside it: A1B7, SP25, Cout26, MQ_OUT[0], Cout33
  // full_adder_1bit A0B7__plus__SP20: pin names not known; wires that end beside it: A0B7, SP20, 1'b0, AC_OUT[7], Cout27

  // Other names for the same wires on the sheet: AC0 = AC_OUT[0]; AC1 = AC_OUT[1]; AC2 = AC_OUT[2]; AC3 = AC_OUT[3];
  //   AC4 = AC_OUT[4]; AC5 = AC_OUT[5]; AC6 = AC_OUT[6]; AC7 = AC_OUT[7]; MQ0 = MQ_OUT[0]; MQ1 = MQ_OUT[1];
  //   MQ2 = MQ_OUT[2]; MQ3 = MQ_OUT[3]; MQ4 = MQ_OUT[4]; MQ5 = MQ_OUT[5]; MQ6 = MQ_OUT[6]; MQ7 = MQ_OUT[7]
endmodule
